# Fritzing sketch sbr_breadboard (saved by Fritzing 0.9.9b)
breadboards: 1

parts:
  VCC1 = Battery
  Part1 = Arduino Nano (Rev3.0) (ICSP)
  Pololu_A4 = Pololu A4988 [package=SO16]
  M2 = Stepper Motor - Bipolar
  M3 = Stepper Motor - Bipolar
  Pololu_A5 = Pololu A4988 [package=SO16]
  Part3 = InvenSense MPU6050
  S1 = Toggle Switch [package=THT]

nets:
  GND: VCC1.-, Part1.GND, Pololu_A4.GND#14, Pololu_A5.GND#14, Part3.GND
  N1: VCC1.+, S1.L2
  N2: Part1.D5, Pololu_A4.RESET
  N3: Part1.D6, Pololu_A4.STEP
  N4: Part1.D7, Pololu_A5.DIR
  N5: Part1.D8, Pololu_A5.STEP
  N6: Part1.VIN, Pololu_A4.VMOT, Pololu_A5.VMOT, S1.COM
  VDD: Part1.5V, Pololu_A4.VDD, Pololu_A5.VDD, Part3.VCC
  N7: Part1.A5, Part3.SCL
  N8: Part1.A4, Part3.SDA
  N9: Pololu_A4.1B, M2.D
  N10: Pololu_A4.1A, M2.B
  N11: Pololu_A4.2A, M2.C
  N12: Pololu_A4.2B, M2.A
  N13: M3.A, Pololu_A5.2B
  N14: M3.C, Pololu_A5.2A
  N15: M3.B, Pololu_A5.1A
  N16: M3.D, Pololu_A5.1B
